# Fritzing sketch GrillLog (saved by Fritzing 0.9.2b)
breadboards: 1

parts:
  Part1 = Arduino Uno (Rev3)
  LCD1 = LCD screen
  R4 = Resistor [tolerance=±5% resistance=1M package=THT]
  SparkFun_WiFi_Shield_-_ESP8266 = Arduino WiFly Shield
  R1 = Resistor [tolerance=±5% resistance=220k package=THT]
  U1 = 2.5mm Audio Jack [package=stereojack2.5mm_smd]
  U2 = 2.5mm Audio Jack [package=stereojack2.5mm_smd]
  R3 = Rotary Potentiometer (Small) [maximum_resistance=10kΩ package=THT]

nets:
  N1: Part1.A0, R1.Pin_0, U2.SLEEVE
  N2: Part1.A1, R4.Pin_0, U1.SLEEVE
  N3: Part1.D8, SparkFun_WiFi_Shield_-_ESP8266.D8
  N4: Part1.D9_PWM, SparkFun_WiFi_Shield_-_ESP8266.D9
  N5: Part1.D11_PWM/MOSI, LCD1.E
  N6: Part1.D12/MISO, LCD1.RS
  GND: Part1.GND, LCD1.VSS, LCD1.R/W, SparkFun_WiFi_Shield_-_ESP8266.GND, U1.LEFT, U2.LEFT, R3.leg1
  N7: Part1.D2, LCD1.DB7
  N8: Part1.D3_PWM, LCD1.DB6
  N9: Part1.D4, LCD1.DB5
  N10: Part1.D5_PWM, LCD1.DB4
  5V: Part1.5V, LCD1.VDD, R4.Pin_1, SparkFun_WiFi_Shield_-_ESP8266.5V, R1.Pin_1, R3.leg2
  N11: LCD1.V0, R3.wiper

notes:
  This is actually a Spark Fun ESP8266 Wifi Shield, not what's pictured
  The ET732 plugs in here
  The generic food probe plugs in here
  Used to adjust LCD Contrast
